# Fritzing sketch Arduino_Nano_and_AD9850_Signal_Generator (saved by Fritzing 0.9.3b)
breadboards: 1

parts:
  Mod1 = DDS AD9850
  Part1 = Arduino Nano (Rev3.0)
  VCC1 = Battery block 9V
  Part2 = LCD1602-I2C
  RE1 = Rotary Encoder [package=THT]
  Part3 = Logic Level Converter

nets:
  VCC: Mod1.VCC, Part1.3V3, Part3.LV
  N1: Mod1.CLK, Part3.TX_LV
  N2: Mod1.FQ, Part3.RX_LV
  N3: Mod1.DATA, Part3.RX2_LV
  N4: Mod1.RST, Part3.TX2_LV
  GND: Mod1.GND, Part1.VIN, VCC1.+, Part2.GND, RE1.EncoderPinC, Part3.GND
  N5: Part1.GND, VCC1.-
  N6: Part1.D2, RE1.EncoderPinB
  N7: Part1.D3, RE1.EncoderPinA
  N8: Part1.D8, Part3.TX_HV
  N9: Part1.D9, Part3.RX_HV
  N10: Part1.D10, Part3.RX2_HV
  N11: Part1.D11/MOSI, Part3.TX2_HV
  5V: Part1.5V, Part2.VCC, Part3.HV
  N12: Part1.A5, Part2.SCL
  N13: Part1.A4, Part2.SDA

notes:
  Arduino Nano and AD9850 Signal Generator

custom parts:
  DDS AD9850: AD9850 DDS Signal Generator Module, frequency range 0 to 40MHz, sine or square wave output, on board 70MHz low pass filter, and 125MHz clock module. https://code.google.com/p/ad9850-arduino/
  LCD1602-I2C: A standard character display, usually with 2x16 characters. Comes in many colors with LCM1602 IIC attached.
